# Fritzing sketch prototype (saved by Fritzing 1.0.5)
perfboards: 1

parts:
  J6 = male pin header, 3 pins [form="♂ (male)"]
  R12 = Resistor [tolerance=±5% power=0.25W resistance=220 package=THT]
  R13 = Resistor [tolerance=±5% power=0.25W resistance=220 package=THT]
  LED6 = LED Red 3mm - Top [color="Green (565nm)" package="3 mm [THT] Top"]
  LED7 = LED Red 3mm - Top [color="Red (633nm)" package="3 mm [THT] Top"]
  C9 = Ceramic Capacitor top view [package="100 mil [THT, multilayer]"]
  U3 = LM 358 Dual Op-Amp [package="DIP8 [THT]"]
  R20 = Resistor [tolerance=±5% power=0.25W resistance=100k package=THT]
  C12 = Ceramic Capacitor top view [package="100 mil [THT, multilayer]"]
  R21 = Resistor [tolerance=±5% power=0.25W resistance=1M package=THT]
  R22 = Resistor [tolerance=±5% power=0.25W resistance=10k package=THT]
  R23 = Resistor [tolerance=±5% power=0.25W resistance=10k package=THT]
  Part3 = Arduino Nano (Rev3.0)
  C13 = Electrolytic Capacitor top view [package="100 mil [THT, electrolytic]"]
  J9 = male pin header, 2 pins [form="♂ (male)"]
  J10 = male pin header, 2 pins [form="♂ (male)"]
  R24 = Resistor [tolerance=±5% power=0.25W resistance=470 package=THT]
  R25 = Resistor [tolerance=±5% power=0.25W resistance=470 package=THT]
  C15 = Ceramic Capacitor top view [package="100 mil [THT, multilayer]"]
  C14 = Electrolytic Capacitor top view [package="100 mil [THT, electrolytic]"]
  J11 = male pin header, 3 pins [form="♂ (male)"]
  R26 = Resistor [tolerance=±5% power=0.25W resistance=10k package=THT]
  J12 = male pin header, 3 pins [form="♂ (male)"]
  C7 = Electrolytic Capacitor top view [package="100 mil [THT, electrolytic]"]

nets:
  N1: J6.pin1, LED7.cathode
  N2: J6.pin2, R22.Pin_1, Part3.5V, J11.pin2, J11.pin3
  N3: J6.pin3, Part3.D2
  N4: R12.Pin_0, LED7.anode
  N5: R12.Pin_1, Part3.D3
  N6: R13.Pin_0, LED6.cathode
  N7: R13.Pin_1, Part3.D4
  N8: LED6.anode, U3.connector3, R23.Pin_0, Part3.GND, C13.-, J9.pin1, C15.0, C14.-, R26.Pin_0, J12.pin1, C7.-
  N9: C9.0, U3.connector2, R21.Pin_1
  N10: C9.1, J9.pin2
  N11: U3.connector0, R20.Pin_0, R25.Pin_1
  N12: U3.connector1, R20.Pin_1, C12.0, J10.pin2
  N13: U3.connector7, C13.+
  N14: R21.Pin_0, R22.Pin_0, R23.Pin_1, C7.+
  N15: Part3.D1/TX, J12.pin3
  N16: Part3.D0/RX, J12.pin2
  N17: Part3.A3, R25.Pin_0, C15.1
  N18: Part3.D13/SCK, J11.pin1, R26.Pin_1
  N19: J10.pin1, R24.Pin_1
  N20: R24.Pin_0, C14.+

custom parts:
  LED Red 3mm - Top: A generic red LED (~1.8V)
  Ceramic Capacitor top view: 100 nF multilayer Ceramic Capacitor breadboard set to top view for perfboard use.
  Electrolytic Capacitor top view: A small electrolytic capacitor breadboard top view for use on perf board
